# Fritzing sketch CPE301L_Schematic (saved by Fritzing 0.9.10b)
breadboards: 1

parts:
  U1 = LCD-16X2 [package=lcd-16x2]
  U2 = DS1307 [package=so08]
  Part1 = Arduino Mega 2560 (Rev3)
  DHT11 = Humidity and Temperature Sensor DHT11
  GREEN_LED = LEDs [package=led10mm]
  YELLOW_LED = LEDs [package=led10mm]
  RED_LED = LEDs [package=led10mm]
  BLUE_LED = LEDs [package=led10mm]
  R1 = Resistor [tolerance=±5% resistance=330 package="0805 [SMD]"]
  R2 = Resistor [tolerance=±5% resistance=330 package="0805 [SMD]"]
  R3 = Resistor [tolerance=±5% resistance=330 package="0805 [SMD]"]
  R4 = Resistor [tolerance=±5% resistance=330 package="0805 [SMD]"]
  Q1 = NPN-Transistor [package="TO92 [THT]"]
  M1 = DC Motor [voltage_(max)=6V voltage_(min)=3V]
  R8 = Rotary Potentiometer (Small) [maximum_resistance=10kΩ knob_status=50% power=0.5W package=THT]
  R9 = Rotary Potentiometer (Small) [maximum_resistance=10kΩ knob_status=50% power=0.5W package=THT]
  R10 = Resistor [tolerance=±0.05% resistance=2.2k power=0.5W package="0805 [SMD]"]
  S2 = Pushbutton [package="[THT]"]
  S3 = Pushbutton [package="[THT]"]
  S4 = Pushbutton [package="[THT]"]
  R11 = Resistor [tolerance=±5% resistance=220 package="0805 [SMD]"]
  R12 = Resistor [tolerance=±5% resistance=220 package="0805 [SMD]"]
  R13 = Resistor [tolerance=±5% resistance=220 package="0805 [SMD]"]
  Part3 = Soil Moisture Sensor
  SM2 = 28BYJ-48 Stepper Motor [part_number=28BYJ-48]
  Driver2 = 28BYJ-48 Driver Module [part_number=ULN2003 package=THT]
  Part4 = Breadboard Power Supply Board SMD

nets:
  GND: U1.VSS, U1.R_W, U1.K, U2.GND, Part1.GND, DHT11.GND_2, GREEN_LED.C, YELLOW_LED.C, RED_LED.C, BLUE_LED.C, M1.pin_2, R8.leg1, R9.leg2, S2.Pin_3, S2.Pin_4, R12.Pin_0, R13.Pin_0, Part3.GND, Driver2.GND, Part4.GND
  VCC: U1.VDD, U2.VCC, Part1.5V, DHT11.Vcc, Q1.C, R8.leg2, R9.leg1, R10.Pin_0, S3.Pin_3, S3.Pin_4, S4.Pin_3, S4.Pin_4, R11.Pin_0, Part3.VCC, Driver2.Vmotor, Part4.VCC
  N1: U1.VO, R9.wiper
  N2: U1.RS, Part1.D9_PWM
  N3: U1.E, Part1.D8_PWM
  N4: U1.DB4, Part1.D5_PWM
  N5: U1.DB5, Part1.D4_PWM
  N6: U1.DB6, Part1.D3_PWM
  N7: U1.DB7, Part1.D7_PWM
  N8: U1.A, R10.Pin_1
  N9: U2.SDA, Part1.D20/SDA, Part1.SDA
  N10: U2.SCL, Part1.D21/SCL, Part1.SCL
  N11: Part1.A15, Part3.SIG
  N12: Part1.A0, R8.wiper
  N13: Part1.D13_PWM, R4.Pin_0
  N14: Part1.D12_PWM, R3.Pin_0
  N15: Part1.D11_PWM, R2.Pin_0
  N16: Part1.D10_PWM, R1.Pin_0
  N17: Part1.D2_PWM, S2.Pin_1, S2.Pin_2
  N18: Part1.D23, Driver2.IN4
  N19: Part1.D25, Driver2.IN2
  N20: Part1.D27, Driver2.IN3
  N21: Part1.D29, Driver2.IN1
  N22: Part1.D30, Q1.B
  N23: Part1.D34, DHT11.Data-signal
  N24: Part1.D42, S3.Pin_1, S3.Pin_2, R12.Pin_1
  N25: Part1.D44, S4.Pin_1, S4.Pin_2, R13.Pin_1
  N26: GREEN_LED.A, R1.Pin_1
  N27: YELLOW_LED.A, R2.Pin_1
  N28: RED_LED.A, R3.Pin_1
  N29: BLUE_LED.A, R4.Pin_1
  N30: Q1.E, M1.pin_1
  N31: SM2.blue-pin, Driver2.blue-pin
  N32: SM2.pink-pin, Driver2.pink-pin
  N33: SM2.yellow-pin, Driver2.yellow-pin
  N34: SM2.orange-pin, Driver2.orange-pin
  N35: SM2.red-pin, Driver2.red-pin

custom parts:
  Humidity and Temperature Sensor DHT11: Digital relative humidity & temperature sensor DHT11
  28BYJ-48 Stepper Motor: Unipolar Stepper Motor 28BYJ-48 Top coil - pink & orange Bottom coil - blue & yellow Common rail - red Connector pins: blue - pink - yellow - orange - red
  28BYJ-48 Driver Module: Generic male header
